# Fritzing sketch protoboard-dado-digital (saved by Fritzing 0.9.6b)
breadboards: 1

parts:
  DI1 = 7-Segment LED Display [package=THT]
  Componente1 = Arduino Uno (Rev3)
  R1 = Resistor [tolerance=±5% power=0.25 resistance=220 package=THT]
  S1 = Pushbutton [package="[THT]"]  # not connected
  R2 = Resistor [tolerance=±5% power=0.25 resistance=220 package=THT]

nets:
  N1: DI1.cathodeE, Componente1.D7
  N2: DI1.cathodeD, Componente1.D6_PWM
  N3: DI1.commAnode#2, R2.Pin_0
  N4: DI1.cathodeC, Componente1.D5_PWM
  N5: DI1.cathodeB, Componente1.D4
  N6: DI1.cathodeA, Componente1.D3_PWM
  N7: DI1.commAnode#7, R1.Pin_1
  N8: Componente1.GND, R1.Pin_0, R2.Pin_1
